# Fritzing sketch schema (saved by Fritzing 0.9.10b)

parts:
  Mod1 = Raspberry Pi Pico
  Part1 = Bluetooth HC-05 Macho
  U1 = WS2812 RGB LED strip
  USBTTL1 = USB TTL Serial Cable
  JP1 = Header 2 [package=r_sw_th]
  LEDCable1 = LED Cable Male
  LEDCable2 = LED Cable Female

nets:
  N1: Mod1.pin_1, Part1.RXD
  N2: Mod1.pin_2, Part1.TXD
  N3: Mod1.pin_4, LEDCable1.Din
  GND: Mod1.pin_33, Mod1.pin_38, Part1.GND, USBTTL1.GND, LEDCable1.GND
  VCC: Mod1.pin_40, Part1.VCC, JP1.2, LEDCable1.+5V
  GND_2: U1.GND, LEDCable2.GND
  VCC_2: U1.VCC, LEDCable2.+5V
  N4: U1.DIN, LEDCable2.Din
  N5: USBTTL1.5V, JP1.1

custom parts:
  Raspberry Pi Pico: Raspberry Pi Pico. Based around the RP2040 microcontroller the Pico is a low cost microcontroller device bringing Raspberry Pi quality, cost, and easy of use to the microcontroller space. Jan 2021, Split part in to two versions: tht (this one) and SMD. This one will drill holes for a .1 in header in pcb to allow plugging in the module as well as providing pads to solder the module to the top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
  WS2812 RGB LED strip: WS2812 strip
  LED Cable Male: LED Cable
  LED Cable Female: LED Cable
